// Logisim project Circuitos.circ as structural Verilog
module Multiplexador_2x1 (
  input  A,
  input  B,
  input  Sel,
  output S
);

  wire and_1_out, and_2_out, not_1_out;

  not not_1 (not_1_out, Sel);
  and and_1 (and_1_out, A, not_1_out);
  and and_2 (and_2_out, B, Sel);
  or or_1 (S, and_1_out, and_2_out);
endmodule

module Somador_Completo (
  input  A,
  input  B,
  input  Vem1,
  output Soma,
  output Vai1
);

  wire and_1_out, and_2_out, and_3_out, xor_1_out;

  xor xor_1 (xor_1_out, A, B);
  and and_1 (and_1_out, A, B);
  and and_2 (and_2_out, Vem1, A);
  and and_3 (and_3_out, Vem1, B);
  xor xor_2 (Soma, xor_1_out, Vem1);
  or or_1 (Vai1, and_1_out, and_2_out, and_3_out);
endmodule

module Multiplexador_4x1 (
  input  _00,
  input  _1,
  input  _2,
  input  _3,
  input  Sel0,
  input  Sel1,
  output out_7
);

  wire multiplexador_2x1_1_s, multiplexador_2x1_2_s;

  Multiplexador_2x1 multiplexador_2x1_1 (.A(_00), .B(_1), .Sel(Sel1), .S(multiplexador_2x1_1_s));
  Multiplexador_2x1 multiplexador_2x1_2 (.A(_2), .B(_3), .Sel(Sel1), .S(multiplexador_2x1_2_s));
  Multiplexador_2x1 multiplexador_2x1_3 (.A(multiplexador_2x1_1_s), .B(multiplexador_2x1_2_s), .Sel(Sel0), .S(out_7));
endmodule

module Multiplexador_8x1 (
  input  _0,
  input  _1,
  input  _2,
  input  _3,
  input  _4,
  input  _5,
  input  _6,
  input  _7,
  input  Sel0,
  input  Sel1,
  input  Sel2,
  output out_12
);

  wire multiplexador_4x1_1_out_7, multiplexador_4x1_2_out_7;

  Multiplexador_4x1 multiplexador_4x1_1 (
    ._00(_0), ._1(_1), ._2(_2), ._3(_3), .Sel0(Sel1), .Sel1(Sel2), .out_7(multiplexador_4x1_1_out_7));
  Multiplexador_4x1 multiplexador_4x1_2 (
    ._00(_4), ._1(_5), ._2(_6), ._3(_7), .Sel0(Sel1), .Sel1(Sel2), .out_7(multiplexador_4x1_2_out_7));
  Multiplexador_2x1 multiplexador_2x1_1 (
    .A(multiplexador_4x1_1_out_7), .B(multiplexador_4x1_2_out_7), .Sel(Sel0), .S(out_12));
endmodule

module Multiplexador_16x1 (
  input  in_1,
  input  in_2,
  input  in_3,
  input  in_4,
  input  in_5,
  input  in_6,
  input  in_7,
  input  in_8,
  input  in_9,
  input  in_10,
  input  in_11,
  input  in_12,
  input  in_13,
  input  in_14,
  input  in_15,
  input  in_16,
  input  Sel0,
  input  Sel0_2,
  input  Sel0_3,
  input  Sel3,
  output out_21
);

  wire multiplexador_8x1_1_out_12, multiplexador_8x1_2_out_12;

  Multiplexador_8x1 multiplexador_8x1_1 (
    ._0(in_1), ._1(in_2), ._2(in_3), ._3(in_4), ._4(in_5), ._5(in_6), ._6(in_7), ._7(in_8), .Sel0(Sel0_2),
    .Sel1(Sel0_3), .Sel2(Sel3), .out_12(multiplexador_8x1_1_out_12));
  Multiplexador_8x1 multiplexador_8x1_2 (
    ._0(in_9), ._1(in_10), ._2(in_11), ._3(in_12), ._4(in_13), ._5(in_14), ._6(in_15), ._7(in_16),
    .Sel0(Sel0_2), .Sel1(Sel0_3), .Sel2(Sel3), .out_12(multiplexador_8x1_2_out_12));
  Multiplexador_2x1 multiplexador_2x1_1 (
    .A(multiplexador_8x1_1_out_12), .B(multiplexador_8x1_2_out_12), .Sel(Sel0), .S(out_21));
endmodule

module Multiplexador_32x1 (
  input  _0,
  input  _1,
  input  _2,
  input  _3,
  input  _4,
  input  _5,
  input  _6,
  input  _7,
  input  _8,
  input  _9,
  input  _10,
  input  _11,
  input  _12,
  input  _13,
  input  _14,
  input  _15,
  input  _16,
  input  _17,
  input  _18,
  input  _19,
  input  _20,
  input  _21,
  input  _22,
  input  _23,
  input  _24,
  input  _25,
  input  _26,
  input  _27,
  input  _28,
  input  _29,
  input  _30,
  input  _31,
  input  Sel0,
  input  Sel1,
  input  Sel2,
  input  Sel3,
  input  Sel4,
  output out_38
);

  wire multiplexador_16x1_1_out_21, multiplexador_16x1_2_out_21;

  Multiplexador_16x1 multiplexador_16x1_1 (
    .in_1(_0), .in_2(_1), .in_3(_2), .in_4(_3), .in_5(_4), .in_6(_5), .in_7(_6), .in_8(_7), .in_9(_8),
    .in_10(_9), .in_11(_10), .in_12(_11), .in_13(_12), .in_14(_13), .in_15(_14), .in_16(_15), .Sel0(Sel1),
    .Sel0_2(Sel2), .Sel0_3(Sel3), .Sel3(Sel4), .out_21(multiplexador_16x1_1_out_21));
  Multiplexador_16x1 multiplexador_16x1_2 (
    .in_1(_16), .in_2(_17), .in_3(_18), .in_4(_19), .in_5(_20), .in_6(_21), .in_7(_22), .in_8(_23),
    .in_9(_24), .in_10(_25), .in_11(_26), .in_12(_27), .in_13(_28), .in_14(_29), .in_15(_30), .in_16(_31),
    .Sel0(Sel1), .Sel0_2(Sel2), .Sel0_3(Sel3), .Sel3(Sel4), .out_21(multiplexador_16x1_2_out_21));
  Multiplexador_2x1 multiplexador_2x1_1 (
    .A(multiplexador_16x1_1_out_21), .B(multiplexador_16x1_2_out_21), .Sel(Sel0), .S(out_38));
endmodule

module \Detector_Subtração  (
  input  [4:0] in_1,
  output Sub
);

  and and_1 (Sub, ~in_1[0], ~in_1[1], in_1[2], ~in_1[3], ~in_1[4]);  // AND_Gate
endmodule

module \Célula_ULA  (
  input  Vem1,
  input  A,
  input  B,
  input  [4:0] \Opção ,
  output Resultado,
  output Vai1
);

  wire and_1_out, detector_slt_1_out_2, \detector_subtração_1_sub , multiplexador_2x1_1_s, nor_1_out,
       not_1_out, or_1_out, or_2_out, somador_completo_1_soma, xor_1_out;

  not not_1 (not_1_out, B);
  Multiplexador_2x1 multiplexador_2x1_1 (.A(B), .B(not_1_out), .Sel(or_1_out), .S(multiplexador_2x1_1_s));
  Somador_Completo somador_completo_1 (
    .A(A), .B(multiplexador_2x1_1_s), .Vem1(Vem1), .Soma(somador_completo_1_soma), .Vai1(Vai1));
  or or_1 (or_1_out, detector_slt_1_out_2, \detector_subtração_1_sub );
  and and_1 (and_1_out, A, B);
  or or_2 (or_2_out, A, B);
  xor xor_1 (xor_1_out, A, B);
  nor nor_1 (nor_1_out, A, B);
  \Detector_Subtração  \detector_subtração_1  (.Sub(\detector_subtração_1_sub ), .in_1(\Opção ));
  Detector__SLT detector_slt_1 (.in_1(\Opção ), .out_2(detector_slt_1_out_2));
  Multiplexador_32x1 multiplexador_32x1_1 (
    ._0(and_1_out), ._1(or_2_out), ._2(xor_1_out), ._3(somador_completo_1_soma),
    ._4(somador_completo_1_soma), ._5(nor_1_out), ._6(somador_completo_1_soma), ._7(somador_completo_1_soma),
    ._8(somador_completo_1_soma), ._9(somador_completo_1_soma), ._10(somador_completo_1_soma),
    ._11(somador_completo_1_soma), ._12(somador_completo_1_soma), ._13(somador_completo_1_soma),
    ._14(somador_completo_1_soma), ._15(somador_completo_1_soma), ._16(somador_completo_1_soma),
    ._17(somador_completo_1_soma), ._18(somador_completo_1_soma), ._19(somador_completo_1_soma),
    ._20(somador_completo_1_soma), ._21(somador_completo_1_soma), ._22(somador_completo_1_soma),
    ._23(somador_completo_1_soma), ._24(somador_completo_1_soma), ._25(somador_completo_1_soma),
    ._26(somador_completo_1_soma), ._27(somador_completo_1_soma), ._28(somador_completo_1_soma),
    ._29(somador_completo_1_soma), ._30(somador_completo_1_soma), ._31(somador_completo_1_soma),
    .Sel0(\Opção [4]), .Sel1(\Opção [3]), .Sel2(\Opção [2]), .Sel3(\Opção [1]), .Sel4(\Opção [0]),
    .out_38(Resultado));
endmodule

module ULA_32bits (
  input  [31:0] A,
  input  [31:0] B,
  input  [4:0] \Opção ,
  output out_4,
  output OverFlowNat,
  output [31:0] Resultado
);

  wire \célula_ula_2_vai1 , \célula_ula_3_vai1 , \célula_ula_4_vai1 , \célula_ula_5_vai1 ,
       \célula_ula_6_vai1 , \célula_ula_7_vai1 , \célula_ula_8_vai1 , \célula_ula_9_vai1 ,
       \célula_ula_10_vai1 , \célula_ula_11_vai1 , \célula_ula_12_vai1 , \célula_ula_13_vai1 ,
       \célula_ula_14_vai1 , \célula_ula_15_vai1 , \célula_ula_16_vai1 , \célula_ula_17_vai1 ,
       \célula_ula_18_vai1 , \célula_ula_19_vai1 , \célula_ula_20_vai1 , \célula_ula_21_vai1 ,
       \célula_ula_22_vai1 , \célula_ula_23_vai1 , \célula_ula_24_vai1 , \célula_ula_25_vai1 ,
       \célula_ula_26_vai1 , \célula_ula_27_vai1 , \célula_ula_28_vai1 , \célula_ula_29_vai1 ,
       \célula_ula_30_vai1 , \célula_ula_31_vai1 , \célula_ula_32_vai1 , detector_slt_1_out_2,
       \detector_subtração_1_sub , Mux_s, or_1_out;
  wire [31:0] \célula_ula_31_resultado ;

  OverFlowInt overflowint_1 (.in_1(\célula_ula_31_resultado [31]), .in_2(B[31]), .in_3(A[31]), .out_4(out_4));
  \Célula_ULA  \célula_ula_1  (
    .Vai1(OverFlowNat), .A(A[31]), .B(B[31]), .\Opção (\Opção ), .Vem1(\célula_ula_2_vai1 ),
    .Resultado(\célula_ula_31_resultado [31]));
  \Célula_ULA  \célula_ula_2  (
    .Vai1(\célula_ula_2_vai1 ), .A(A[30]), .B(B[30]), .\Opção (\Opção ), .Vem1(\célula_ula_3_vai1 ),
    .Resultado(\célula_ula_31_resultado [30]));
  \Célula_ULA  \célula_ula_3  (
    .Vai1(\célula_ula_3_vai1 ), .A(A[29]), .B(B[29]), .\Opção (\Opção ), .Vem1(\célula_ula_4_vai1 ),
    .Resultado(\célula_ula_31_resultado [29]));
  \Célula_ULA  \célula_ula_4  (
    .Vai1(\célula_ula_4_vai1 ), .A(A[28]), .B(B[28]), .\Opção (\Opção ), .Vem1(\célula_ula_5_vai1 ),
    .Resultado(\célula_ula_31_resultado [28]));
  \Célula_ULA  \célula_ula_5  (
    .Vai1(\célula_ula_5_vai1 ), .A(A[27]), .B(B[27]), .\Opção (\Opção ), .Vem1(\célula_ula_6_vai1 ),
    .Resultado(\célula_ula_31_resultado [27]));
  \Célula_ULA  \célula_ula_6  (
    .Vai1(\célula_ula_6_vai1 ), .A(A[26]), .B(B[26]), .\Opção (\Opção ), .Vem1(\célula_ula_7_vai1 ),
    .Resultado(\célula_ula_31_resultado [26]));
  \Célula_ULA  \célula_ula_7  (
    .Vai1(\célula_ula_7_vai1 ), .A(A[25]), .B(B[25]), .\Opção (\Opção ), .Vem1(\célula_ula_8_vai1 ),
    .Resultado(\célula_ula_31_resultado [25]));
  \Célula_ULA  \célula_ula_8  (
    .Vai1(\célula_ula_8_vai1 ), .A(A[24]), .B(B[24]), .\Opção (\Opção ), .Vem1(\célula_ula_9_vai1 ),
    .Resultado(\célula_ula_31_resultado [24]));
  \Célula_ULA  \célula_ula_9  (
    .Vai1(\célula_ula_9_vai1 ), .A(A[23]), .B(B[23]), .\Opção (\Opção ), .Vem1(\célula_ula_10_vai1 ),
    .Resultado(\célula_ula_31_resultado [23]));
  \Célula_ULA  \célula_ula_10  (
    .Vai1(\célula_ula_10_vai1 ), .A(A[22]), .B(B[22]), .\Opção (\Opção ), .Vem1(\célula_ula_12_vai1 ),
    .Resultado(\célula_ula_31_resultado [22]));
  \Célula_ULA  \célula_ula_11  (
    .Vai1(\célula_ula_11_vai1 ), .A(A[20]), .B(B[20]), .\Opção (\Opção ), .Vem1(\célula_ula_13_vai1 ),
    .Resultado(\célula_ula_31_resultado [20]));
  \Célula_ULA  \célula_ula_12  (
    .Vai1(\célula_ula_12_vai1 ), .A(A[21]), .B(B[21]), .\Opção (\Opção ), .Vem1(\célula_ula_11_vai1 ),
    .Resultado(\célula_ula_31_resultado [21]));
  \Célula_ULA  \célula_ula_13  (
    .Vai1(\célula_ula_13_vai1 ), .A(A[19]), .B(B[19]), .\Opção (\Opção ), .Vem1(\célula_ula_14_vai1 ),
    .Resultado(\célula_ula_31_resultado [19]));
  \Célula_ULA  \célula_ula_14  (
    .Vai1(\célula_ula_14_vai1 ), .A(A[18]), .B(B[18]), .\Opção (\Opção ), .Vem1(\célula_ula_15_vai1 ),
    .Resultado(\célula_ula_31_resultado [18]));
  \Célula_ULA  \célula_ula_15  (
    .Vai1(\célula_ula_15_vai1 ), .A(A[17]), .B(B[17]), .\Opção (\Opção ), .Vem1(\célula_ula_16_vai1 ),
    .Resultado(\célula_ula_31_resultado [17]));
  \Célula_ULA  \célula_ula_16  (
    .Vai1(\célula_ula_16_vai1 ), .A(A[16]), .B(B[16]), .\Opção (\Opção ), .Vem1(\célula_ula_17_vai1 ),
    .Resultado(\célula_ula_31_resultado [16]));
  \Célula_ULA  \célula_ula_17  (
    .Vai1(\célula_ula_17_vai1 ), .A(A[15]), .B(B[15]), .\Opção (\Opção ), .Vem1(\célula_ula_18_vai1 ),
    .Resultado(\célula_ula_31_resultado [15]));
  \Célula_ULA  \célula_ula_18  (
    .Vai1(\célula_ula_18_vai1 ), .A(A[14]), .B(B[14]), .\Opção (\Opção ), .Vem1(\célula_ula_19_vai1 ),
    .Resultado(\célula_ula_31_resultado [14]));
  \Célula_ULA  \célula_ula_19  (
    .Vai1(\célula_ula_19_vai1 ), .A(A[13]), .B(B[13]), .\Opção (\Opção ), .Vem1(\célula_ula_20_vai1 ),
    .Resultado(\célula_ula_31_resultado [13]));
  \Célula_ULA  \célula_ula_20  (
    .Vai1(\célula_ula_20_vai1 ), .A(A[12]), .B(B[12]), .\Opção (\Opção ), .Vem1(\célula_ula_21_vai1 ),
    .Resultado(\célula_ula_31_resultado [12]));
  \Célula_ULA  \célula_ula_21  (
    .Vai1(\célula_ula_21_vai1 ), .A(A[11]), .B(B[11]), .\Opção (\Opção ), .Vem1(\célula_ula_22_vai1 ),
    .Resultado(\célula_ula_31_resultado [11]));
  \Célula_ULA  \célula_ula_22  (
    .Vai1(\célula_ula_22_vai1 ), .A(A[10]), .B(B[10]), .\Opção (\Opção ), .Vem1(\célula_ula_24_vai1 ),
    .Resultado(\célula_ula_31_resultado [10]));
  \Célula_ULA  \célula_ula_23  (
    .Vai1(\célula_ula_23_vai1 ), .A(A[8]), .B(B[8]), .\Opção (\Opção ), .Vem1(\célula_ula_25_vai1 ),
    .Resultado(\célula_ula_31_resultado [8]));
  \Célula_ULA  \célula_ula_24  (
    .Vai1(\célula_ula_24_vai1 ), .A(A[9]), .B(B[9]), .\Opção (\Opção ), .Vem1(\célula_ula_23_vai1 ),
    .Resultado(\célula_ula_31_resultado [9]));
  \Célula_ULA  \célula_ula_25  (
    .Vai1(\célula_ula_25_vai1 ), .A(A[7]), .B(B[7]), .\Opção (\Opção ), .Vem1(\célula_ula_26_vai1 ),
    .Resultado(\célula_ula_31_resultado [7]));
  \Célula_ULA  \célula_ula_26  (
    .Vai1(\célula_ula_26_vai1 ), .A(A[6]), .B(B[6]), .\Opção (\Opção ), .Vem1(\célula_ula_28_vai1 ),
    .Resultado(\célula_ula_31_resultado [6]));
  \Célula_ULA  \célula_ula_27  (
    .Vai1(\célula_ula_27_vai1 ), .A(A[4]), .B(B[4]), .\Opção (\Opção ), .Vem1(\célula_ula_29_vai1 ),
    .Resultado(\célula_ula_31_resultado [4]));
  \Célula_ULA  \célula_ula_28  (
    .Vai1(\célula_ula_28_vai1 ), .A(A[5]), .B(B[5]), .\Opção (\Opção ), .Vem1(\célula_ula_27_vai1 ),
    .Resultado(\célula_ula_31_resultado [5]));
  \Célula_ULA  \célula_ula_29  (
    .Vai1(\célula_ula_29_vai1 ), .A(A[3]), .B(B[3]), .\Opção (\Opção ), .Vem1(\célula_ula_30_vai1 ),
    .Resultado(\célula_ula_31_resultado [3]));
  MUX_32_bits mux_32_bits_1 (
    .in_3(detector_slt_1_out_2), .B({{31{1'b0}}, \célula_ula_31_resultado [31]}),
    .A(\célula_ula_31_resultado ), .Resultado(Resultado));
  \Detector_Subtração  \detector_subtração_1  (.Sub(\detector_subtração_1_sub ), .in_1(\Opção ));
  Detector__SLT detector_slt_1 (.in_1(\Opção ), .out_2(detector_slt_1_out_2));
  \Célula_ULA  \célula_ula_30  (
    .Vai1(\célula_ula_30_vai1 ), .A(A[2]), .B(B[2]), .\Opção (\Opção ), .Vem1(\célula_ula_32_vai1 ),
    .Resultado(\célula_ula_31_resultado [2]));
  or or_1 (or_1_out, \detector_subtração_1_sub , detector_slt_1_out_2);
  \Célula_ULA  \célula_ula_31  (
    .Vai1(\célula_ula_31_vai1 ), .A(A[0]), .B(B[0]), .\Opção (\Opção ), .Vem1(Mux_s),
    .Resultado(\célula_ula_31_resultado [0]));
  \Célula_ULA  \célula_ula_32  (
    .Vai1(\célula_ula_32_vai1 ), .A(A[1]), .B(B[1]), .\Opção (\Opção ), .Vem1(\célula_ula_31_vai1 ),
    .Resultado(\célula_ula_31_resultado [1]));
  Multiplexador_2x1 Mux (.A(1'b0), .B(1'b1), .Sel(or_1_out), .S(Mux_s));
endmodule

module OverFlowInt (
  input  in_1,
  input  in_2,
  input  in_3,
  output out_4
);

  wire xnor_1_out, xor_1_out;

  and and_1 (out_4, xnor_1_out, xor_1_out);
  xnor xnor_1 (xnor_1_out, in_1, in_2);
  xor xor_1 (xor_1_out, in_3, in_2);
endmodule

module Detector__SLT (
  input  [4:0] in_1,
  output out_2
);

  and and_1 (out_2, ~in_1[0], in_1[1], in_1[2], ~in_1[3], ~in_1[4]);  // AND_Gate
endmodule

module Maior__menor__igual (
  input  A,
  input  B,
  output IGUAL,
  output MAIOR,
  output MENOR
);

  xnor xnor_1 (IGUAL, A, B);
  and and_1 (MAIOR, A, ~B);  // AND_Gate
  and and_2 (MENOR, ~A, B);  // AND_Gate
endmodule

module ULA (
  input  [3:0] A,
  input  [3:0] B,
  input  [4:0] \Opção ,
  output [3:0] Resultado
);

  wire \célula_ula_2_vai1 , \célula_ula_3_vai1 , \célula_ula_4_vai1 , detector_slt_1_out_2,
       \detector_subtração_1_sub , multiplexador_2x1_1_s, mux_32_bits_1_p1, mux_32_bits_1_p2, or_1_out;
  wire [3:0] \célula_ula_4_resultado ;

  \Célula_ULA  \célula_ula_1  (
    .A(A[3]), .B(B[3]), .\Opção (\Opção ), .Vem1(\célula_ula_2_vai1 ), .Resultado(\célula_ula_4_resultado [3]));  // open: Vai1
  \Célula_ULA  \célula_ula_2  (
    .Vai1(\célula_ula_2_vai1 ), .A(A[2]), .B(B[2]), .\Opção (\Opção ), .Vem1(\célula_ula_3_vai1 ),
    .Resultado(\célula_ula_4_resultado [2]));
  \Célula_ULA  \célula_ula_3  (
    .Vai1(\célula_ula_3_vai1 ), .A(A[1]), .B(B[1]), .\Opção (\Opção ), .Vem1(\célula_ula_4_vai1 ),
    .Resultado(\célula_ula_4_resultado [1]));
  \Célula_ULA  \célula_ula_4  (
    .Vai1(\célula_ula_4_vai1 ), .A(A[0]), .B(B[0]), .\Opção (\Opção ), .Vem1(multiplexador_2x1_1_s),
    .Resultado(\célula_ula_4_resultado [0]));
  Multiplexador_2x1 multiplexador_2x1_1 (.A(1'b0), .B(1'b1), .Sel(or_1_out), .S(multiplexador_2x1_1_s));
  // MUX_32_bits mux_32_bits_1: pin names not known; wires that end beside it: mux_32_bits_1_p1, mux_32_bits_1_p2, Resultado
  \Detector_Subtração  \detector_subtração_1  (.Sub(\detector_subtração_1_sub ), .in_1(\Opção ));
  Detector__SLT detector_slt_1 (.in_1(\Opção ), .out_2(detector_slt_1_out_2));
  or or_1 (or_1_out, \detector_subtração_1_sub , detector_slt_1_out_2);
endmodule

module MUX_32_bits (
  input  [31:0] B,
  input  [31:0] A,
  input  in_3,
  output [31:0] Resultado
);

  Multiplexador_2x1 multiplexador_2x1_1 (.A(A[0]), .B(B[0]), .Sel(in_3), .S(Resultado[0]));
  Multiplexador_2x1 multiplexador_2x1_2 (.A(A[1]), .B(B[1]), .Sel(in_3), .S(Resultado[1]));
  Multiplexador_2x1 multiplexador_2x1_3 (.A(A[2]), .B(B[2]), .Sel(in_3), .S(Resultado[2]));
  Multiplexador_2x1 multiplexador_2x1_4 (.A(A[3]), .B(B[3]), .Sel(in_3), .S(Resultado[3]));
  Multiplexador_2x1 multiplexador_2x1_5 (.A(A[4]), .B(B[4]), .Sel(in_3), .S(Resultado[4]));
  Multiplexador_2x1 multiplexador_2x1_6 (.A(A[5]), .B(B[5]), .Sel(in_3), .S(Resultado[5]));
  Multiplexador_2x1 multiplexador_2x1_7 (.A(A[6]), .B(B[6]), .Sel(in_3), .S(Resultado[6]));
  Multiplexador_2x1 multiplexador_2x1_8 (.A(A[7]), .B(B[7]), .Sel(in_3), .S(Resultado[7]));
  Multiplexador_2x1 multiplexador_2x1_9 (.A(A[8]), .B(B[8]), .Sel(in_3), .S(Resultado[8]));
  Multiplexador_2x1 multiplexador_2x1_10 (.A(A[9]), .B(B[9]), .Sel(in_3), .S(Resultado[9]));
  Multiplexador_2x1 multiplexador_2x1_11 (.A(A[10]), .B(B[10]), .Sel(in_3), .S(Resultado[10]));
  Multiplexador_2x1 multiplexador_2x1_12 (.A(A[11]), .B(B[11]), .Sel(in_3), .S(Resultado[11]));
  Multiplexador_2x1 multiplexador_2x1_13 (.A(A[12]), .B(B[12]), .Sel(in_3), .S(Resultado[12]));
  Multiplexador_2x1 multiplexador_2x1_14 (.A(A[13]), .B(B[13]), .Sel(in_3), .S(Resultado[13]));
  Multiplexador_2x1 multiplexador_2x1_15 (.A(A[14]), .B(B[14]), .Sel(in_3), .S(Resultado[14]));
  Multiplexador_2x1 multiplexador_2x1_16 (.A(A[15]), .B(B[15]), .Sel(in_3), .S(Resultado[15]));
  Multiplexador_2x1 multiplexador_2x1_17 (.A(A[16]), .B(B[16]), .Sel(in_3), .S(Resultado[16]));
  Multiplexador_2x1 multiplexador_2x1_18 (.A(A[17]), .B(B[17]), .Sel(in_3), .S(Resultado[17]));
  Multiplexador_2x1 multiplexador_2x1_19 (.A(A[18]), .B(B[18]), .Sel(in_3), .S(Resultado[18]));
  Multiplexador_2x1 multiplexador_2x1_20 (.A(A[19]), .B(B[19]), .Sel(in_3), .S(Resultado[19]));
  Multiplexador_2x1 multiplexador_2x1_21 (.A(A[20]), .B(B[20]), .Sel(in_3), .S(Resultado[20]));
  Multiplexador_2x1 multiplexador_2x1_22 (.A(A[21]), .B(B[21]), .Sel(in_3), .S(Resultado[21]));
  Multiplexador_2x1 multiplexador_2x1_23 (.A(A[22]), .B(B[22]), .Sel(in_3), .S(Resultado[22]));
  Multiplexador_2x1 multiplexador_2x1_24 (.A(A[23]), .B(B[23]), .Sel(in_3), .S(Resultado[23]));
  Multiplexador_2x1 multiplexador_2x1_25 (.A(A[24]), .B(B[24]), .Sel(in_3), .S(Resultado[24]));
  Multiplexador_2x1 multiplexador_2x1_26 (.A(A[25]), .B(B[25]), .Sel(in_3), .S(Resultado[25]));
  Multiplexador_2x1 multiplexador_2x1_27 (.A(A[26]), .B(B[26]), .Sel(in_3), .S(Resultado[26]));
  Multiplexador_2x1 multiplexador_2x1_28 (.A(A[27]), .B(B[27]), .Sel(in_3), .S(Resultado[27]));
  Multiplexador_2x1 multiplexador_2x1_29 (.A(A[28]), .B(B[28]), .Sel(in_3), .S(Resultado[28]));
  Multiplexador_2x1 multiplexador_2x1_30 (.A(A[29]), .B(B[29]), .Sel(in_3), .S(Resultado[29]));
  Multiplexador_2x1 multiplexador_2x1_31 (.A(A[30]), .B(B[30]), .Sel(in_3), .S(Resultado[30]));
  Multiplexador_2x1 multiplexador_2x1_32 (.A(A[31]), .B(B[31]), .Sel(in_3), .S(Resultado[31]));
endmodule

module FlipFlop_D (
  input  D,
  input  CLK,
  input  Clear,
  output Q,
  output Q1
);

  wire and_1_out, and_2_out, nand_1_out, nand_2_out, nand_3_out, not_1_out;

  not not_1 (not_1_out, D);
  and and_1 (and_1_out, D, CLK);
  nand nand_1 (nand_1_out, CLK, not_1_out);
  nand nand_2 (nand_2_out, CLK, not_1_out);
  nand nand_3 (nand_3_out, nand_1_out, Clear);
  and and_2 (and_2_out, nand_2_out, nand_3_out);
  nand nand_4 (Q, ~and_1_out, Q1);  // NAND_Gate
  nand nand_5 (Q1, Q, and_2_out);
endmodule

module Registrador (
  input  [31:0] DataIn,
  input  CLK,
  input  Clear,
  output [31:0] DataOut
);

  wire flipflop_d_4_q1;

  FlipFlop_D flipflop_d_1 (.D(DataIn[31]), .CLK(CLK), .Clear(Clear), .Q(DataOut[31]));  // open: Q1
  FlipFlop_D flipflop_d_2 (.D(DataIn[30]), .CLK(CLK), .Clear(Clear), .Q(DataOut[30]));  // open: Q1
  FlipFlop_D flipflop_d_3 (.D(DataIn[29]), .CLK(CLK), .Clear(Clear), .Q(DataOut[29]));  // open: Q1
  FlipFlop_D flipflop_d_4 (.D(DataIn[28]), .CLK(CLK), .Clear(Clear), .Q(DataOut[28]), .Q1(flipflop_d_4_q1));
  FlipFlop_D flipflop_d_5 (.D(DataIn[27]), .CLK(CLK), .Clear(Clear), .Q(DataOut[27]));  // open: Q1
  FlipFlop_D flipflop_d_6 (.D(DataIn[26]), .CLK(CLK), .Clear(Clear), .Q(DataOut[26]));  // open: Q1
  FlipFlop_D flipflop_d_7 (.D(DataIn[25]), .CLK(CLK), .Clear(Clear), .Q(DataOut[25]));  // open: Q1
  FlipFlop_D flipflop_d_8 (.D(DataIn[24]), .CLK(CLK), .Clear(Clear), .Q(DataOut[24]));  // open: Q1
  FlipFlop_D flipflop_d_9 (.D(DataIn[23]), .CLK(CLK), .Clear(Clear), .Q(DataOut[23]));  // open: Q1
  FlipFlop_D flipflop_d_10 (.D(DataIn[22]), .CLK(CLK), .Clear(Clear), .Q(DataOut[22]));  // open: Q1
  FlipFlop_D flipflop_d_11 (.D(DataIn[21]), .CLK(CLK), .Clear(Clear), .Q(DataOut[21]));  // open: Q1
  FlipFlop_D flipflop_d_12 (.D(DataIn[20]), .CLK(CLK), .Clear(Clear), .Q(DataOut[20]));  // open: Q1
  FlipFlop_D flipflop_d_13 (.D(DataIn[19]), .CLK(CLK), .Clear(Clear), .Q(DataOut[19]));  // open: Q1
  FlipFlop_D flipflop_d_14 (.D(DataIn[18]), .CLK(CLK), .Clear(Clear), .Q(DataOut[18]));  // open: Q1
  FlipFlop_D flipflop_d_15 (.D(DataIn[17]), .CLK(CLK), .Clear(Clear), .Q(DataOut[17]));  // open: Q1
  FlipFlop_D flipflop_d_16 (.D(DataIn[16]), .CLK(CLK), .Clear(Clear), .Q(DataOut[16]));  // open: Q1
  FlipFlop_D flipflop_d_17 (.D(DataIn[15]), .CLK(CLK), .Clear(Clear), .Q(DataOut[15]));  // open: Q1
  FlipFlop_D flipflop_d_18 (.D(DataIn[14]), .CLK(CLK), .Clear(Clear), .Q(DataOut[14]));  // open: Q1
  FlipFlop_D flipflop_d_19 (.D(DataIn[13]), .CLK(CLK), .Clear(Clear), .Q(DataOut[13]));  // open: Q1
  FlipFlop_D flipflop_d_20 (.D(DataIn[12]), .CLK(CLK), .Clear(Clear), .Q(DataOut[12]));  // open: Q1
  FlipFlop_D flipflop_d_21 (.D(DataIn[11]), .CLK(CLK), .Clear(Clear), .Q(DataOut[11]));  // open: Q1
  FlipFlop_D flipflop_d_22 (.D(DataIn[10]), .CLK(CLK), .Clear(Clear), .Q(DataOut[10]));  // open: Q1
  FlipFlop_D flipflop_d_23 (.D(DataIn[9]), .CLK(CLK), .Clear(Clear), .Q(DataOut[9]));  // open: Q1
  FlipFlop_D flipflop_d_24 (.D(DataIn[8]), .CLK(CLK), .Clear(Clear), .Q(DataOut[8]));  // open: Q1
  FlipFlop_D flipflop_d_25 (.D(DataIn[7]), .CLK(CLK), .Clear(Clear), .Q(DataOut[7]));  // open: Q1
  FlipFlop_D flipflop_d_26 (.D(DataIn[6]), .CLK(CLK), .Clear(Clear), .Q(DataOut[6]));  // open: Q1
  FlipFlop_D flipflop_d_27 (.D(DataIn[5]), .CLK(CLK), .Clear(Clear), .Q(DataOut[5]));  // open: Q1
  FlipFlop_D flipflop_d_28 (.D(DataIn[4]), .CLK(CLK), .Clear(Clear), .Q(DataOut[4]));  // open: Q1
  FlipFlop_D flipflop_d_29 (.D(DataIn[3]), .CLK(CLK), .Clear(Clear), .Q(DataOut[3]));  // open: Q1
  FlipFlop_D flipflop_d_30 (.D(DataIn[2]), .CLK(CLK), .Clear(Clear), .Q(DataOut[2]));  // open: Q1
  FlipFlop_D flipflop_d_31 (.D(DataIn[1]), .CLK(CLK), .Clear(Clear), .Q(DataOut[1]));  // open: Q1
  FlipFlop_D flipflop_d_32 (.D(DataIn[0]), .CLK(CLK), .Clear(Clear), .Q(DataOut[0]));  // open: Q1
endmodule

module Registrador2 (
  input  [31:0] DataIn,
  input  CLK,
  input  Clear,
  output [31:0] DataOut
);

  D_Flip_Flop d_ff_1 (.clk(CLK), .D(DataIn[31]), .Q(DataOut[31]), .reset(Clear));  // open: Qn, preset, en
  D_Flip_Flop d_ff_2 (.clk(CLK), .D(DataIn[30]), .Q(DataOut[30]), .reset(Clear));  // open: Qn, preset, en
  D_Flip_Flop d_ff_3 (.clk(CLK), .D(DataIn[29]), .Q(DataOut[29]), .reset(Clear));  // open: Qn, preset, en
  D_Flip_Flop d_ff_4 (.clk(CLK), .D(DataIn[28]), .Q(DataOut[28]), .reset(Clear));  // open: Qn, preset, en
  D_Flip_Flop d_ff_5 (.clk(CLK), .D(DataIn[27]), .Q(DataOut[27]), .reset(Clear));  // open: Qn, preset, en
  D_Flip_Flop d_ff_6 (.clk(CLK), .D(DataIn[25]), .Q(DataOut[25]), .reset(Clear));  // open: Qn, preset, en
  D_Flip_Flop d_ff_7 (.clk(CLK), .D(DataIn[26]), .Q(DataOut[26]), .reset(Clear));  // open: Qn, preset, en
  D_Flip_Flop d_ff_8 (.clk(CLK), .D(DataIn[24]), .Q(DataOut[24]), .reset(Clear));  // open: Qn, preset, en
  D_Flip_Flop d_ff_9 (.clk(CLK), .D(DataIn[23]), .Q(DataOut[23]), .reset(Clear));  // open: Qn, preset, en
  D_Flip_Flop d_ff_10 (.clk(CLK), .D(DataIn[22]), .Q(DataOut[22]), .reset(Clear));  // open: Qn, preset, en
  D_Flip_Flop d_ff_11 (.clk(CLK), .D(DataIn[21]), .Q(DataOut[21]), .reset(Clear));  // open: Qn, preset, en
  D_Flip_Flop d_ff_12 (.clk(CLK), .D(DataIn[20]), .Q(DataOut[20]), .reset(Clear));  // open: Qn, preset, en
  D_Flip_Flop d_ff_13 (.clk(CLK), .D(DataIn[19]), .Q(DataOut[19]), .reset(Clear));  // open: Qn, preset, en
  D_Flip_Flop d_ff_14 (.clk(CLK), .D(DataIn[18]), .Q(DataOut[18]), .reset(Clear));  // open: Qn, preset, en
  D_Flip_Flop d_ff_15 (.clk(CLK), .D(DataIn[17]), .Q(DataOut[17]), .reset(Clear));  // open: Qn, preset, en
  D_Flip_Flop d_ff_16 (.clk(CLK), .D(DataIn[16]), .Q(DataOut[16]), .reset(Clear));  // open: Qn, preset, en
  D_Flip_Flop d_ff_17 (.clk(CLK), .D(DataIn[15]), .Q(DataOut[15]));  // open: Qn, preset, en, reset
  D_Flip_Flop d_ff_18 (.clk(CLK), .D(DataIn[14]), .Q(DataOut[14]), .reset(Clear));  // open: Qn, preset, en
  D_Flip_Flop d_ff_19 (.clk(CLK), .D(DataIn[13]), .Q(DataOut[13]), .reset(Clear));  // open: Qn, preset, en
  D_Flip_Flop d_ff_20 (.clk(CLK), .D(DataIn[12]), .Q(DataOut[12]), .reset(Clear));  // open: Qn, preset, en
  D_Flip_Flop d_ff_21 (.clk(CLK), .D(DataIn[11]), .Q(DataOut[11]), .reset(Clear));  // open: Qn, preset, en
  D_Flip_Flop d_ff_22 (.clk(CLK), .D(DataIn[10]), .Q(DataOut[10]), .reset(Clear));  // open: Qn, preset, en
  D_Flip_Flop d_ff_23 (.clk(CLK), .D(DataIn[9]), .Q(DataOut[9]), .reset(Clear));  // open: Qn, preset, en
  D_Flip_Flop d_ff_24 (.clk(CLK), .D(DataIn[8]), .Q(DataOut[8]), .reset(Clear));  // open: Qn, preset, en
  D_Flip_Flop d_ff_25 (.clk(CLK), .D(DataIn[7]), .Q(DataOut[7]), .reset(Clear));  // open: Qn, preset, en
  D_Flip_Flop d_ff_26 (.clk(CLK), .D(DataIn[6]), .Q(DataOut[6]), .reset(Clear));  // open: Qn, preset, en
  D_Flip_Flop d_ff_27 (.clk(CLK), .D(DataIn[5]), .Q(DataOut[5]), .reset(Clear));  // open: Qn, preset, en
  D_Flip_Flop d_ff_28 (.clk(CLK), .D(DataIn[4]), .Q(DataOut[4]), .reset(Clear));  // open: Qn, preset, en
  D_Flip_Flop d_ff_29 (.clk(CLK), .D(DataIn[3]), .Q(DataOut[3]), .reset(Clear));  // open: Qn, preset, en
  D_Flip_Flop d_ff_30 (.clk(CLK), .D(DataIn[2]), .Q(DataOut[2]), .reset(Clear));  // open: Qn, preset, en
  D_Flip_Flop d_ff_31 (.clk(CLK), .D(DataIn[1]), .Q(DataOut[1]), .reset(Clear));  // open: Qn, preset, en
  D_Flip_Flop d_ff_32 (.clk(CLK), .D(DataIn[0]), .Q(DataOut[0]), .reset(Clear));  // open: Qn, preset, en
endmodule

module Banco_Registrador_2 (
  input  [4:0] Registro2,
  input  LImpar,
  input  Salvar,
  input  [4:0] Destino,
  input  [4:0] Registro1,
  input  [31:0] Entrada,
  output [31:0] \Saída1 ,
  output [31:0] \Saída2 
);

  wire undriven, undriven_2, undriven_3, undriven_4, undriven_5, undriven_6, undriven_7, undriven_8,
       undriven_9, undriven_10, undriven_11, undriven_12, undriven_13, undriven_14, undriven_15, undriven_16,
       undriven_17, undriven_18, undriven_19, undriven_20, undriven_21, undriven_22, undriven_23,
       undriven_24, undriven_25, undriven_26, undriven_27, undriven_28, undriven_29, undriven_30,
       undriven_31, undriven_32;
  wire [31:0] multiplexer_3_out, registrador2_1_dataout, registrador2_2_dataout, registrador2_3_dataout,
       registrador2_4_dataout, registrador2_5_dataout, registrador2_6_dataout, registrador2_7_dataout,
       registrador2_8_dataout, registrador2_9_dataout, registrador2_10_dataout, registrador2_11_dataout,
       registrador2_12_dataout, registrador2_13_dataout, registrador2_14_dataout, registrador2_15_dataout,
       registrador2_16_dataout, registrador2_17_dataout, registrador2_18_dataout, registrador2_19_dataout,
       registrador2_20_dataout, registrador2_21_dataout, registrador2_22_dataout, registrador2_23_dataout,
       registrador2_24_dataout, registrador2_25_dataout, registrador2_26_dataout, registrador2_27_dataout,
       registrador2_28_dataout, registrador2_29_dataout, registrador2_30_dataout, registrador2_31_dataout,
       registrador2_32_dataout;

  Multiplexer #(.select(5), .enable("false")) multiplexer_1 (
    .in0(undriven), .in1(undriven_2), .in2(undriven_3), .in3(undriven_4), .in4(undriven_5), .in5(undriven_6),
    .in6(undriven_7), .in7(undriven_8), .in8(undriven_9), .in9(undriven_10), .in10(undriven_11),
    .in11(undriven_12), .in12(undriven_13), .in13(undriven_14), .in14(undriven_15), .in15(undriven_16),
    .in16(undriven_17), .in17(undriven_18), .in18(undriven_19), .in19(undriven_20), .in20(undriven_21),
    .in21(undriven_22), .in22(undriven_23), .in23(undriven_24), .in24(undriven_25), .in25(undriven_26),
    .in26(undriven_27), .in27(undriven_28), .in28(undriven_29), .in29(undriven_30), .in30(undriven_31),
    .in31(undriven_32), .out(Salvar), .sel(Destino));
  Registrador2 registrador2_1 (.DataIn(Entrada), .CLK(undriven), .Clear(LImpar), .DataOut(registrador2_1_dataout));
  Registrador2 registrador2_2 (.DataIn(Entrada), .CLK(undriven_2), .Clear(LImpar), .DataOut(registrador2_2_dataout));
  Registrador2 registrador2_3 (.DataIn(Entrada), .CLK(undriven_3), .Clear(LImpar), .DataOut(registrador2_3_dataout));
  Registrador2 registrador2_4 (.DataIn(Entrada), .CLK(undriven_4), .Clear(LImpar), .DataOut(registrador2_4_dataout));
  Registrador2 registrador2_5 (.DataIn(Entrada), .CLK(undriven_5), .Clear(LImpar), .DataOut(registrador2_5_dataout));
  Registrador2 registrador2_6 (.DataIn(Entrada), .CLK(undriven_6), .Clear(LImpar), .DataOut(registrador2_6_dataout));
  Registrador2 registrador2_7 (.DataIn(Entrada), .CLK(undriven_7), .Clear(LImpar), .DataOut(registrador2_7_dataout));
  Registrador2 registrador2_8 (.DataIn(Entrada), .CLK(undriven_8), .Clear(LImpar), .DataOut(registrador2_8_dataout));
  Registrador2 registrador2_9 (.DataIn(Entrada), .CLK(undriven_9), .Clear(LImpar), .DataOut(registrador2_9_dataout));
  Registrador2 registrador2_10 (.DataIn(Entrada), .CLK(undriven_10), .Clear(LImpar), .DataOut(registrador2_10_dataout));
  Registrador2 registrador2_11 (.DataIn(Entrada), .CLK(undriven_11), .Clear(LImpar), .DataOut(registrador2_11_dataout));
  Registrador2 registrador2_12 (.DataIn(Entrada), .CLK(undriven_12), .Clear(LImpar), .DataOut(registrador2_12_dataout));
  Registrador2 registrador2_13 (.DataIn(Entrada), .CLK(undriven_13), .Clear(LImpar), .DataOut(registrador2_13_dataout));
  Registrador2 registrador2_14 (.DataIn(Entrada), .CLK(undriven_14), .Clear(LImpar), .DataOut(registrador2_14_dataout));
  Registrador2 registrador2_15 (.DataIn(Entrada), .CLK(undriven_15), .Clear(LImpar), .DataOut(registrador2_15_dataout));
  Registrador2 registrador2_16 (.DataIn(Entrada), .CLK(undriven_16), .Clear(LImpar), .DataOut(registrador2_16_dataout));
  Registrador2 registrador2_17 (.DataIn(Entrada), .CLK(undriven_17), .Clear(LImpar), .DataOut(registrador2_17_dataout));
  Registrador2 registrador2_18 (.DataIn(Entrada), .CLK(undriven_18), .Clear(LImpar), .DataOut(registrador2_18_dataout));
  Registrador2 registrador2_19 (.DataIn(Entrada), .CLK(undriven_19), .Clear(LImpar), .DataOut(registrador2_19_dataout));
  Registrador2 registrador2_20 (.DataIn(Entrada), .CLK(undriven_20), .Clear(LImpar), .DataOut(registrador2_20_dataout));
  Registrador2 registrador2_21 (.DataIn(Entrada), .CLK(undriven_21), .Clear(LImpar), .DataOut(registrador2_21_dataout));
  Registrador2 registrador2_22 (.DataIn(Entrada), .CLK(undriven_22), .Clear(LImpar), .DataOut(registrador2_22_dataout));
  Registrador2 registrador2_23 (.DataIn(Entrada), .CLK(undriven_23), .Clear(LImpar), .DataOut(registrador2_23_dataout));
  Registrador2 registrador2_24 (.DataIn(Entrada), .CLK(undriven_24), .Clear(LImpar), .DataOut(registrador2_24_dataout));
  Registrador2 registrador2_25 (.DataIn(Entrada), .CLK(undriven_25), .Clear(LImpar), .DataOut(registrador2_25_dataout));
  Registrador2 registrador2_26 (.DataIn(Entrada), .CLK(undriven_26), .Clear(LImpar), .DataOut(registrador2_26_dataout));
  Registrador2 registrador2_27 (.DataIn(Entrada), .CLK(undriven_27), .Clear(LImpar), .DataOut(registrador2_27_dataout));
  Registrador2 registrador2_28 (.DataIn(Entrada), .CLK(undriven_28), .Clear(LImpar), .DataOut(registrador2_28_dataout));
  Registrador2 registrador2_29 (.DataIn(Entrada), .CLK(undriven_29), .Clear(LImpar), .DataOut(registrador2_29_dataout));
  Registrador2 registrador2_30 (.DataIn(Entrada), .CLK(undriven_30), .Clear(LImpar), .DataOut(registrador2_30_dataout));
  Registrador2 registrador2_31 (.DataIn(Entrada), .CLK(undriven_31), .Clear(LImpar), .DataOut(registrador2_31_dataout));
  Registrador2 registrador2_32 (.DataIn(Entrada), .CLK(undriven_32), .Clear(LImpar), .DataOut(registrador2_32_dataout));
  Multiplexer #(.select(5), .width(32), .enable("false")) multiplexer_2 (
    .in0(registrador2_1_dataout), .in1(registrador2_2_dataout), .in2(registrador2_3_dataout),
    .in3(registrador2_4_dataout), .in4(registrador2_5_dataout), .in5(registrador2_6_dataout),
    .in6(registrador2_7_dataout), .in7(registrador2_8_dataout), .in8(registrador2_9_dataout),
    .in9(registrador2_10_dataout), .in10(registrador2_11_dataout), .in11(registrador2_12_dataout),
    .in12(registrador2_13_dataout), .in13(registrador2_14_dataout), .in14(registrador2_15_dataout),
    .in15(registrador2_16_dataout), .in16(registrador2_17_dataout), .in17(registrador2_18_dataout),
    .in18(registrador2_19_dataout), .in19(registrador2_20_dataout), .in20(registrador2_21_dataout),
    .in21(registrador2_22_dataout), .in22(registrador2_23_dataout), .in23(registrador2_24_dataout),
    .in24(registrador2_25_dataout), .in25(registrador2_26_dataout), .in26(registrador2_27_dataout),
    .in27(registrador2_28_dataout), .in28(registrador2_29_dataout), .in29(registrador2_30_dataout),
    .in30(registrador2_31_dataout), .in31(registrador2_32_dataout), .out(\Saída1 ), .sel(Registro2));
  Multiplexer #(.select(5), .width(32), .enable("false")) multiplexer_3 (
    .in0(registrador2_1_dataout), .in1(registrador2_2_dataout), .in2(registrador2_3_dataout),
    .in3(registrador2_4_dataout), .in4(registrador2_5_dataout), .in5(registrador2_6_dataout),
    .in6(registrador2_7_dataout), .in7(registrador2_8_dataout), .in8(registrador2_9_dataout),
    .in9(registrador2_10_dataout), .in10(registrador2_11_dataout), .in11(registrador2_12_dataout),
    .in12(registrador2_13_dataout), .in13(registrador2_14_dataout), .in14(registrador2_15_dataout),
    .in15(registrador2_16_dataout), .in16(registrador2_17_dataout), .in17(registrador2_18_dataout),
    .in18(registrador2_19_dataout), .in19(registrador2_20_dataout), .in20(registrador2_21_dataout),
    .in21(registrador2_22_dataout), .in22(registrador2_23_dataout), .in23(registrador2_24_dataout),
    .in24(registrador2_25_dataout), .in25(registrador2_26_dataout), .in26(registrador2_27_dataout),
    .in27(registrador2_28_dataout), .in28(registrador2_29_dataout), .in29(registrador2_30_dataout),
    .in30(registrador2_31_dataout), .in31(registrador2_32_dataout), .out(multiplexer_3_out), .sel(Registro1));
endmodule
